// Logisim project lab09part1.circ as structural Verilog: 1 circuit, main circuit main
module main (
  input  A1,
  input  B1,
  input  A0,
  input  B0,
  output Y
);

  wire xor_1_out, xor_3_out;

  xor xor_1 (xor_1_out, A1, B1);
  xor xor_2 (Y, xor_1_out, xor_3_out);
  xor xor_3 (xor_3_out, A0, B0);
endmodule
